# Fritzing sketch backpack_ping_multi (saved by Fritzing 0.9.2b)

parts:
  Part1 = Arduino Nano (Rev3.0)
  Part2 = SRF05 Ultrasonic Rangefinder
  Part3 = Arduino Uno (Rev3)
  Part4 = SRF05 Ultrasonic Rangefinder

nets:
  GND: Part1.GND, Part2.GND, Part3.GND, Part4.GND
  N1: Part1.D8, Part2.Trig, Part2.Echo
  N2: Part1.D9, Part4.Trig, Part4.Echo
  5V: Part1.5V, Part2.VCC, Part3.5V, Part4.VCC
  N3: Part1.A5, Part3.A5/SCL
  N4: Part1.A4, Part3.A4/SDA
